// Digital circuit alu-32b-final.dig as structural Verilog
module alu_32b_final (
  input  [31:0] A,
  input  nz0,
  input  [31:0] B,
  input  [7:0] Opcode,
  input  [4:0] control,
  input  [31:0] REG_C,
  input  cin_sel,
  input  FLAG_C,
  output vout,
  output zout,
  output nzout,
  output nout,
  output [31:0] Out,
  output cout
);

  wire c7, c15, c23, nz1, nz2, nz3;
  wire [7:0] c0_7, c8_15, c16_23, c24_31;
  wire [31:0] multiplexer_1_out;

  Multiplexer #(.Bits(32)) multiplexer_1 (
    .sel(cin_sel), .in_0({{31{1'b0}}, FLAG_C}), .in_1(32'h1), .out(multiplexer_1_out));
  Multiplexer #(.Bits(32)) multiplexer_2 (
    .sel(control[4]), .in_0(multiplexer_1_out), .in_1(REG_C), .out({c24_31, c16_23, c8_15, c0_7}));
  not not_1 (zout, nzout);
  alu_8b_final Cell_0 (
    .opcode(Opcode), .control(control), .A(A[7:0]), .B(B[7:0]), .C(c0_7), .nz_in(nz0), .cin(c0_7[0]),
    .out(Out[7:0]), .nz_out(nz1), .cout(c7));  // open: vout, zout, n
  alu_8b_final Cell_1 (
    .opcode(Opcode), .control(control), .A(A[15:8]), .B(B[15:8]), .C(c8_15), .nz_in(nz2), .cin(c7),
    .out(Out[15:8]), .nz_out(nz3), .cout(c15));  // open: vout, zout, n
  alu_8b_final Cell_2 (
    .opcode(Opcode), .control(control), .A(A[23:16]), .B(B[23:16]), .C(c16_23), .nz_in(nz1), .cin(c15),
    .out(Out[23:16]), .nz_out(nz2), .cout(c23));  // open: vout, zout, n
  alu_8b_final Cell_3 (
    .opcode(Opcode), .control(control), .A(A[31:24]), .B(B[31:24]), .C(c24_31), .nz_in(nz3), .cin(c23),
    .out(Out[31:24]), .vout(vout), .nz_out(nzout), .n(nout), .cout(cout));  // open: zout

  // Other names for the same wires on the sheet: a0_7[7:0] = A[7:0]; a8_15[7:0] = A[15:8]; a16_23[7:0] = A[23:16];
  //   a24_31[7:0] = A[31:24]; b0_7[7:0] = B[7:0]; b8_15[7:0] = B[15:8]; b16_23[7:0] = B[23:16];
  //   b24_31[7:0] = B[31:24]; ceff[31:0] = {c24_31, c16_23, c8_15, c0_7}; cin0 = c0_7[0]; asel = control[0];
  //   ainv = control[1]; bsel = control[2]; binv = control[3]; csel = control[4]; FLAG_C32[0] = FLAG_C;
  //   out0_7[7:0] = Out[7:0]; out8_15[7:0] = Out[15:8]; out16_23[7:0] = Out[23:16]; out24_31[7:0] = Out[31:24]

  // Notes on the sheet:
  //   A: default 9
  //   B: default 20
  //   Opcode: default 150
  //   control: default 21
endmodule

/* Test case Exhaustive 91 Ops Test:
A nz0 B REG_C Opcode control cin-sel FLAG_C Out vout zout nzout nout cout
0x9E250D03 1 0xECEFE37B 0x888417A5 0x96 5 0 0 0x8B14F07E 0 0 1 1 1
0x922BADB0 0 0x95F628F2 0xBB5D75B8 0x96 5 0 0 0x2821D6A2 1 0 1 0 1
0xC6737B8B 1 0xD30A286E 0x5531AE6D 0x96 5 0 0 0x997DA3F9 0 0 1 1 1
0xA28718E5 1 0xCA2410FD 0x5C1ED35F 0x96 5 0 0 0x6CAB29E2 1 0 1 0 1
0x643CB56D 0 0xFE03E76F 0xB2767375 0x96 5 0 0 0x62409CDC 0 0 1 0 1
0xC2F40B30 1 0xA801CF8B 0xDD23F7B6 0x96 5 0 1 0x6AF5DABC 1 0 1 0 1
0x1BFA530D 1 0x6CECC258 0xD2083355 0x96 5 0 1 0x88E71566 1 0 1 1 0
0xE66EB118 1 0x10BA53D8 0x8161701F 0x96 5 0 1 0xF72904F1 0 0 1 1 0
0xE369AB3D 1 0x67518339 0x67433A86 0x96 5 0 1 0x4ABB2E77 0 0 1 0 1
0xA9EB7262 1 0x0490392A 0xD51F25E6 0x96 5 0 1 0xAE7BAB8D 0 0 1 1 0
0x982E524E 0 0x1E5876BF 0x75FFBFF5 0x96 5 0 1 0xB686C90E 0 0 1 1 0
0xF522DFDC 1 0x2BD4E7AB 0xCBB452AE 0x96 5 0 1 0x20F7C788 0 0 1 0 1
0xADE42791 1 0xB0C751A5 0xEBF96C57 0x96 5 0 1 0x5EAB7937 1 0 1 0 1
0x9A795FF6 0 0x43CD9D75 0xCDD25AA1 0x96 5 0 1 0xDE46FD6C 0 0 1 1 0
0x8C39D6BB 0 0x113A972F 0xA36AEC07 0x96 5 0 1 0x9D746DEB 0 0 1 1 0
0x127E2CC8 0 0x684FF42B 0xF666C60F 0x96 1 0 1 0x127E2CC9 0 0 1 0 0
0xACF40C45 0 0x0463522C 0xA28F38BD 0x96 1 0 1 0xACF40C46 0 0 1 1 0
0x32700980 0 0x1AC66DEA 0x48F0E642 0x96 1 0 1 0x32700981 0 0 1 0 0
0x73CBC7FD 1 0xBFC5C2A1 0xEAA1C37B 0x96 1 0 1 0x73CBC7FE 0 0 1 0 0
0x0330F04D 1 0xCB9FD223 0xEFD6A13E 0x96 1 0 1 0x0330F04E 0 0 1 0 0
0x6EA29BD0 0 0x9275BAB2 0xCA5976A6 0x96 4 0 1 0x9275BAB3 0 0 1 1 0
0x8CB33116 1 0x0BBBAED5 0xC6A7BA53 0x96 4 0 1 0x0BBBAED6 0 0 1 0 0
0xD932B231 0 0xE433713D 0x36B1CC9F 0x96 4 0 1 0xE433713E 0 0 1 1 0
0x8771830D 0 0x86D6B717 0x87485FF5 0x96 4 0 1 0x86D6B718 0 0 1 1 0
0xC67B74E2 1 0xA9A29C4C 0x0CE941CC 0x96 4 0 1 0xA9A29C4D 0 0 1 1 0
0xB421B5BA 1 0xBC8B306F 0x95714C91 0x96 9 0 0 0xB421B5B9 0 0 1 1 1
0xF9307A71 1 0xE6171071 0x0649D0EB 0x96 9 0 0 0xF9307A70 0 0 1 1 1
0x8AD5F511 1 0xC08EEEE9 0xA779CFE5 0x96 9 0 0 0x8AD5F510 0 0 1 1 1
0xBC15526A 1 0x8EF1FB25 0xCC638D6A 0x96 9 0 0 0xBC155269 0 0 1 1 1
0x4303F922 0 0x11190839 0xB5710CDB 0x96 9 0 0 0x4303F921 0 0 1 0 1
0xF2A57B17 0 0x0F140E3F 0xE7545280 0x96 6 0 0 0x0F140E3E 0 0 1 0 1
0x50E84FEE 0 0xD1EA37FC 0x1413B58C 0x96 6 0 0 0xD1EA37FB 0 0 1 1 1
0x70806354 1 0xF3E1F4FC 0x8A59AED2 0x96 6 0 0 0xF3E1F4FB 0 0 1 1 1
0xE0A94677 0 0x0DBBFF09 0x8DF6073D 0x96 6 0 0 0x0DBBFF08 0 0 1 0 1
0x6D53855D 0 0x59667DF9 0x9B3C8F00 0x96 6 0 0 0x59667DF8 0 0 1 0 1
0x6E10D8AC 0 0x4999DEE8 0xBDB78C3F 0x96 3 0 1 0x91EF2754 0 0 1 1 0
0x0E531C17 1 0xA24898EF 0x7618F5FD 0x96 3 0 1 0xF1ACE3E9 0 0 1 1 0
0x6164B99C 1 0x118344EB 0x355AC876 0x96 3 0 1 0x9E9B4664 0 0 1 1 0
0xA83BC84C 1 0xAD46E79A 0xA4CC68AA 0x96 3 0 1 0x57C437B4 0 0 1 0 0
0xB7A60EC1 0 0x36B87E69 0x310791BB 0x96 3 0 1 0x4859F13F 0 0 1 0 0
0x7BEBC774 1 0x6451FADD 0x9CF8D97F 0x96 12 0 1 0x9BAE0523 0 0 1 1 0
0x8D85B315 0 0x40BC0884 0x28E3D333 0x96 12 0 1 0xBF43F77C 0 0 1 1 0
0xB61E20F7 1 0xFDC95E56 0xD7B9BA35 0x96 12 0 1 0x0236A1AA 0 0 1 0 0
0x649866E0 1 0x9FD67893 0x31CCDCBD 0x96 12 0 1 0x6029876D 0 0 1 0 0
0xEF320F9E 1 0x28BA4DB2 0xB7C8CF35 0x96 12 0 1 0xD745B24E 0 0 1 1 0
0x9F39D060 1 0xB29983BC 0xA111B92E 0x96 3 0 0 0x60C62F9F 0 0 1 0 0
0x0A14680D 0 0x07BD9483 0x8A3B319F 0x96 3 0 0 0xF5EB97F2 0 0 1 1 0
0xA42CA3E6 1 0x6FFEDC96 0x4E939F7B 0x96 3 0 0 0x5BD35C19 0 0 1 0 0
0xC7E29A0A 1 0x670370E8 0xDFBE3B62 0x96 3 0 0 0x381D65F5 0 0 1 0 0
0x399FCFD6 1 0xEAD13C41 0x4E26B0B8 0x96 3 0 0 0xC6603029 0 0 1 1 0
0x9483F548 1 0x6109DFB9 0xF7375D41 0x96 12 0 0 0x9EF62046 0 0 1 1 0
0x24E1BA2D 1 0x9FA88BBA 0xD202751C 0x96 12 0 0 0x60577445 0 0 1 0 0
0xC339627C 1 0xBF0D1338 0x3C9921ED 0x96 12 0 0 0x40F2ECC7 0 0 1 0 0
0xD02819D9 1 0xB556EC05 0x15F909CC 0x96 12 0 0 0x4AA913FA 0 0 1 0 0
0xB1AC56A2 0 0x00BC9D0C 0x57ADF7DB 0x96 12 0 0 0xFF4362F3 0 0 1 1 0
0xD75CE2E2 1 0xEE87E8A2 0x4674252D 0x96 1 0 0 0xD75CE2E2 0 0 1 1 0
0x86F40248 1 0xD1CC2302 0x981D1BAA 0x96 1 0 0 0x86F40248 0 0 1 1 0
0xFF195E1B 1 0x23B8EF17 0x0982694D 0x96 1 0 0 0xFF195E1B 0 0 1 1 0
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*/
