// Digital circuit alu-4b-final.dig as structural Verilog
module alu_4b_final (
  input  [3:0] A,
  input  [3:0] B,
  input  [7:0] lutA,
  input  [3:0] C,
  input  cin,
  input  [7:0] lutB,
  output [3:0] Out,
  output cout,
  output sum3,
  output aeff3,
  output beff3
);

  wire x0, x1, x2, y0, y1, y2;

  alu_1b_final alu_1b_final_1 (.OPCODE(lutB), .A(A[0]), .B(B[0]), .C(C[0]), .MUX_OUT(x0));
  alu_1b_final alu_1b_final_2 (.OPCODE(lutB), .A(A[1]), .B(B[1]), .C(C[1]), .MUX_OUT(x1));
  alu_1b_final alu_1b_final_3 (.OPCODE(lutB), .A(A[2]), .B(B[2]), .C(C[2]), .MUX_OUT(x2));
  alu_1b_final alu_1b_final_4 (.OPCODE(lutB), .A(A[3]), .B(B[3]), .C(C[3]), .MUX_OUT(aeff3));
  _74283 _74283_1 (
    .pin1(Out[1]), .pin2(y1), .pin3(x1), .pin4(Out[0]), .pin5(x0), .pin6(y0), .pin7(cin), .pin8(1'b0),
    .pin9(cout), .pin10(Out[3]), .pin11(beff3), .pin12(aeff3), .pin13(Out[2]), .pin14(x2), .pin15(y2),
    .pin16(1'b1));
  alu_1b_final alu_1b_final_5 (.OPCODE(lutA), .A(A[0]), .B(B[0]), .C(C[0]), .MUX_OUT(y0));
  alu_1b_final alu_1b_final_6 (.OPCODE(lutA), .A(A[1]), .B(B[1]), .C(C[1]), .MUX_OUT(y1));
  alu_1b_final alu_1b_final_7 (.OPCODE(lutA), .A(A[2]), .B(B[2]), .C(C[2]), .MUX_OUT(y2));
  alu_1b_final alu_1b_final_8 (.OPCODE(lutA), .A(A[3]), .B(B[3]), .C(C[3]), .MUX_OUT(beff3));

  assign sum3 = Out[3];

  // Other names for the same wires on the sheet: x3 = aeff3; y3 = beff3

  // Notes on the sheet:
  //   A: default 5
  //   B: default 3
  //   lutA: default 170
  //   lutB: default 170
endmodule
