// Digital circuit alu-8b-final.dig as structural Verilog
module alu_8b_final (
  input  [7:0] opcode,
  input  asel,
  input  [7:0] A,
  input  [7:0] B,
  input  [7:0] C,
  input  ainv,
  input  bsel,
  input  binv,
  output [7:0] out,
  output [7:0] P,
  output [7:0] G
);

  alu_1b_final alu_1b_final_1 (
    .OPCODE(opcode), .A(A[0]), .B(B[0]), .C(C[0]), .Asel(asel), .Bsel(bsel), .A_inv(ainv), .B_inv(binv),
    .MUX_OUT(out[0]), .G(G[0]), .P(P[0]));
  alu_1b_final alu_1b_final_2 (
    .OPCODE(opcode), .A(A[1]), .B(B[1]), .C(C[1]), .Asel(asel), .Bsel(bsel), .A_inv(ainv), .B_inv(binv),
    .MUX_OUT(out[1]), .G(G[1]), .P(P[1]));
  alu_1b_final alu_1b_final_3 (
    .OPCODE(opcode), .A(A[2]), .B(B[2]), .C(C[2]), .Asel(asel), .Bsel(bsel), .A_inv(ainv), .B_inv(binv),
    .MUX_OUT(out[2]), .G(G[2]), .P(P[2]));
  alu_1b_final alu_1b_final_4 (
    .OPCODE(opcode), .A(A[3]), .B(B[3]), .C(C[3]), .Asel(asel), .Bsel(bsel), .A_inv(ainv), .B_inv(binv),
    .MUX_OUT(out[3]), .G(G[3]), .P(P[3]));
  alu_1b_final alu_1b_final_5 (
    .OPCODE(opcode), .A(A[4]), .B(B[4]), .C(C[4]), .Asel(asel), .Bsel(bsel), .A_inv(ainv), .B_inv(binv),
    .MUX_OUT(out[4]), .G(G[4]), .P(P[4]));
  alu_1b_final alu_1b_final_6 (
    .OPCODE(opcode), .A(A[5]), .B(B[5]), .C(C[5]), .Asel(asel), .Bsel(bsel), .A_inv(ainv), .B_inv(binv),
    .MUX_OUT(out[5]), .G(G[5]), .P(P[5]));
  alu_1b_final alu_1b_final_7 (
    .OPCODE(opcode), .A(A[6]), .B(B[6]), .C(C[6]), .Asel(asel), .Bsel(bsel), .A_inv(ainv), .B_inv(binv),
    .MUX_OUT(out[6]), .G(G[6]), .P(P[6]));
  alu_1b_final alu_1b_final_8 (
    .OPCODE(opcode), .A(A[7]), .B(B[7]), .C(C[7]), .Asel(asel), .Bsel(bsel), .A_inv(ainv), .B_inv(binv),
    .MUX_OUT(out[7]), .G(G[7]), .P(P[7]));

  // Notes on the sheet:
  //   opcode: default 150
  //   asel: default 17
  //   A: default 6
  //   B: default 1
  //   C: default 1
  //   ainv: default 1
  //   bsel: default 1
  //   binv: default 1
endmodule
