// Digital circuit alu-control.dig as structural Verilog
module alu_control (
  input  [9:0] op,
  output [7:0] alu_op,
  output [3:0] alu_pre,
  output [1:0] cin_sel
);

  wire [7:6] alu_shift_control_d;

  ROM #(.bigEndian("true"), .AddrBits(10), .Bits(8)) alu_control (.A(op), .sel(1'b1), .D(alu_op));
  ROM #(.bigEndian("true"), .AddrBits(10), .Bits(8)) alu_shift_control (
    .A(op), .sel(1'b1), .D({alu_shift_control_d, cin_sel, alu_pre}));

  // Other names for the same wires on the sheet: ir_opcode[9:0] = op

  // Notes on the sheet:
  //   op: default 48
  //   alu_control loads alu_control_1.hex
  //   alu_shift_control loads alu_control_2.hex
endmodule
