// Digital circuit byte-lane-decoder.dig as structural Verilog
module byte_lane_decoder (
  input  [31:0] mem_in,
  input  [1:0] sel_in,
  input  [31:0] io_data_in,
  input  [1:0] c_addr_msb2,
  output [31:0] mem_out
);

  Multiplexer #(.Selector_Bits(4), .Bits(32)) multiplexer_1 (
    .sel({c_addr_msb2, sel_in}), .in_0(mem_in),
    .in_1({mem_in[7:0], mem_in[15:8], mem_in[23:16], mem_in[31:24]}), .in_2(io_data_in), .in_3({32{1'b0}}),
    .in_4({{25{mem_in[7]}}, mem_in[6:0]}), .in_5({{25{mem_in[15]}}, mem_in[14:8]}),
    .in_6({{25{mem_in[23]}}, mem_in[22:16]}), .in_7({{25{mem_in[31]}}, mem_in[30:24]}),
    .in_8({{24{1'b0}}, mem_in[7:0]}), .in_9({{24{1'b0}}, mem_in[15:8]}), .in_10({{24{1'b0}}, mem_in[23:16]}),
    .in_11({{24{1'b0}}, mem_in[31:24]}), .in_12({{17{mem_in[15]}}, mem_in[14:0]}),
    .in_13({{17{mem_in[31]}}, mem_in[30:16]}), .in_14({{16{1'b0}}, mem_in[15:0]}),
    .in_15({{16{1'b0}}, mem_in[31:16]}), .out(mem_out));

  // Other names for the same wires on the sheet: sel[3:0] = {c_addr_msb2, sel_in}; io_in[31:0] = io_data_in;
  //   byte0[7:0] = mem_in[7:0]; byte01[15:0] = mem_in[15:0]; in0[31:0] = {{25{mem_in[7]}}, mem_in[6:0]};
  //   in4[7:0] = mem_in[7:0]; in8[31:0] = {{17{mem_in[15]}}, mem_in[14:0]}; in10[15:0] = mem_in[15:0];
  //   in12[31:0] = {mem_in[7:0], mem_in[15:8], mem_in[23:16], mem_in[31:24]}; d7__gt_24[23:0] = {24{mem_in[7]}};
  //   byte1[7:0] = mem_in[15:8]; in1[31:0] = {{25{mem_in[15]}}, mem_in[14:8]}; in5[7:0] = mem_in[15:8];
  //   d15__gt_16[15:0] = {16{mem_in[15]}}; d15__gt_24[23:0] = {24{mem_in[15]}}; byte2[7:0] = mem_in[23:16];
  //   byte23[15:0] = mem_in[31:16]; in2[31:0] = {{25{mem_in[23]}}, mem_in[22:16]}; in6[7:0] = mem_in[23:16];
  //   in9[31:0] = {{17{mem_in[31]}}, mem_in[30:16]}; in11[15:0] = mem_in[31:16]; d23__gt_24[23:0] = {24{mem_in[23]}};
  //   byte3[7:0] = mem_in[31:24]; in3[31:0] = {{25{mem_in[31]}}, mem_in[30:24]}; in7[7:0] = mem_in[31:24];
  //   d31__gt_16[15:0] = {16{mem_in[31]}}; d31__gt_24[23:0] = {24{mem_in[31]}}

  // Notes on the sheet:
  //   mem_in: default 3735928559
  //   io_data_in: default 2882343476
  //   BYTE-EXTRACT
  //   S-BYTE
  //   S-HALF-LOW-HIGH
  //   Z-BYTE
  //   Z-HALF-LOW-HIGH
endmodule
