// Digital circuit mem-io-control.dig as structural Verilog
module mem_io_control (
  input  [9:0] op,
  output bank_en,
  output flags_we,
  output mem_rd,
  output mem_wr,
  output [3:0] byte_sel
);

  ROM #(.bigEndian("true"), .AddrBits(10), .Bits(8)) mem_io_control (
    .A(op), .sel(1'b1), .D({byte_sel, mem_wr, mem_rd, flags_we, bank_en}));

  // Other names for the same wires on the sheet: ir_opcode[9:0] = op

  // Notes on the sheet:
  //   op: default 48
  //   mem_io_control loads mem_io_control.hex
endmodule
