// Digital circuit mul-div.dig as structural Verilog
module mul_div (
);

  wire [31:0] undriven, undriven_2;

  Mul #(.Bits(16)) mul_1 (.a(undriven[15:0]), .b(undriven_2[15:0]));  // open: mul
  Div #(.Bits(32)) div_1 (.a(undriven), .b(undriven_2));  // open: q, r
  // Pins of 16 and 32 bits meet at undriven
  // Pins of 16 and 32 bits meet at undriven_2
endmodule
