// Digital circuit vga.dig as structural Verilog
module vga (
  input  [23:0] mem_addr,
  input  [31:0] mem_din,
  input  [12:0] disp_read_addr,
  input  clk,
  output [31:0] disp_data_out
);

  wire not_1_out, vga_en;

  not not_1 (not_1_out, mem_addr[19]);
  and and_1 (vga_en, not_1_out, mem_addr[20], mem_addr[21]);
  RAMDualAccess #(.AddrBits(13), .Bits(16)) ramdualaccess_1 (
    .str(vga_en), .C(clk), .ld(1'b1), .A1(mem_addr[12:0]), .Din1(mem_din[31:16]), .A2(disp_read_addr),
    .D2(disp_data_out[15:0]));  // open: D1
  RAMDualAccess #(.AddrBits(13), .Bits(16)) ramdualaccess_2 (
    .str(vga_en), .C(clk), .ld(1'b1), .A1(mem_addr[12:0]), .Din1(mem_din[15:0]), .A2(disp_read_addr),
    .D2(disp_data_out[31:16]));  // open: D1

  // Other names for the same wires on the sheet: disp_write_addr[12:0] = mem_addr[12:0];
  //   disp_data_in0[15:0] = mem_din[15:0]; disp_data_in1[15:0] = mem_din[31:16]

  // Notes on the sheet:
  //   mem_addr: default 3145728
endmodule
